// Logisim project hw5pr1.circ as structural Verilog
module MyXOR (
  input  Input,
  input  Input_2,
  output Output
);

  wire and_1_out, and_2_out, not_1_out, not_2_out;

  not not_1 (not_1_out, Input);
  not not_2 (not_2_out, Input_2);
  and and_1 (and_1_out, not_1_out, Input_2);
  and and_2 (and_2_out, Input, not_2_out);
  or or_1 (Output, and_1_out, and_2_out);
endmodule

module FullAdder (
  input  X,
  input  Y,
  input  CarryIn,
  output sum,
  output CarryOut
);

  wire and_1_out, and_2_out, and_3_out, and_4_out, and_5_out, and_6_out, and_7_out, and_8_out, not_1_out,
       not_2_out, not_3_out;

  not not_1 (not_1_out, X);
  not not_2 (not_2_out, CarryIn);
  not not_3 (not_3_out, Y);
  and and_1 (and_1_out, not_1_out, not_3_out, CarryIn);
  and and_2 (and_2_out, not_1_out, Y, not_2_out);
  and and_3 (and_3_out, X, not_3_out, not_2_out);
  and and_4 (and_4_out, X, Y, CarryIn);
  and and_5 (and_5_out, not_1_out, Y, CarryIn);
  and and_6 (and_6_out, X, not_3_out, CarryIn);
  and and_7 (and_7_out, X, Y, not_2_out);
  and and_8 (and_8_out, X, Y, CarryIn);
  or or_1 (sum, and_1_out, and_2_out, and_3_out, and_4_out);
  or or_2 (CarryOut, and_5_out, and_6_out, and_7_out, and_8_out);
endmodule

module _4_bit_Ripple_Carry_Adder (
  input  Y3,
  input  Y2,
  input  Y1,
  input  Y0,
  input  X3,
  input  X2,
  input  X1,
  input  X0,
  output Sum4,
  output Sum3,
  output Sum2,
  output Sum1,
  output Sum0
);

  wire fulladder_2_carryout, fulladder_3_carryout, fulladder_4_carryout;

  FullAdder fulladder_1 (.X(X3), .Y(Y3), .CarryIn(fulladder_2_carryout), .sum(Sum3), .CarryOut(Sum4));
  FullAdder fulladder_2 (.X(X2), .Y(Y2), .CarryIn(fulladder_3_carryout), .sum(Sum2), .CarryOut(fulladder_2_carryout));
  FullAdder fulladder_3 (.X(X1), .Y(Y1), .CarryIn(fulladder_4_carryout), .sum(Sum1), .CarryOut(fulladder_3_carryout));
  FullAdder fulladder_4 (.X(X0), .Y(Y0), .CarryIn(1'b0), .sum(Sum0), .CarryOut(fulladder_4_carryout));
endmodule

module _4_bit_Multiplier (
  input  Y3,
  input  Y2,
  input  Y1,
  input  Y0,
  input  X3,
  input  X2,
  input  X1,
  input  X0,
  output Z7,
  output Z6,
  output Z5,
  output Z4,
  output Z3,
  output Z2,
  output Z1,
  output Z0
);


  // Notes on the sheet:
  //   factor (4 bits)
  //   See the problem for details on this hint: perhaps build a 4x1-bit multiplier first!
  //   second factor (4 bits)
  //   product (7 bits)
  //   most significant (highest) bit
  //   least significant (lowest) bit
endmodule

module _3by2_divider (
  input  Y2,
  input  Y1,
  input  Y0,
  input  X1,
  input  X0,
  output Z2,
  output Z1,
  output Z0,
  output Error
);


  // Notes on the sheet:
  //   Dividend (3 bits: Y2 Y1 Y0)
  //   Divisor (2 bits: X1 X0)
  //   Quotient (4 bits: Z2 Z1 Z0 and Error)
endmodule
