// Logisim project hw5pr4.circ as structural Verilog
module MyXOR (
  input  Input,
  input  Input_2,
  output Output
);

  wire and_1_out, and_2_out, not_1_out, not_2_out;

  not not_1 (not_1_out, Input);
  not not_2 (not_2_out, Input_2);
  and and_1 (and_1_out, not_1_out, Input_2);
  and and_2 (and_2_out, Input, not_2_out);
  or or_1 (Output, and_1_out, and_2_out);
endmodule

module FullAdder (
  input  X,
  input  Y,
  input  CarryIn,
  output sum,
  output CarryOut
);

  wire and_1_out, and_2_out, and_3_out, and_4_out, and_5_out, and_6_out, and_7_out, and_8_out, not_1_out,
       not_2_out, not_3_out;

  not not_1 (not_1_out, X);
  not not_2 (not_2_out, CarryIn);
  not not_3 (not_3_out, Y);
  and and_1 (and_1_out, not_1_out, not_3_out, CarryIn);
  and and_2 (and_2_out, not_1_out, Y, not_2_out);
  and and_3 (and_3_out, X, not_3_out, not_2_out);
  and and_4 (and_4_out, X, Y, CarryIn);
  and and_5 (and_5_out, not_1_out, Y, CarryIn);
  and and_6 (and_6_out, X, not_3_out, CarryIn);
  and and_7 (and_7_out, X, Y, not_2_out);
  and and_8 (and_8_out, X, Y, CarryIn);
  or or_1 (sum, and_1_out, and_2_out, and_3_out, and_4_out);
  or or_2 (CarryOut, and_5_out, and_6_out, and_7_out, and_8_out);
endmodule

module _4_bit_Ripple_Carry_Adder (
  input  Y3,
  input  Y2,
  input  Y1,
  input  Y0,
  input  X3,
  input  X2,
  input  X1,
  input  X0,
  output Sum4,
  output Sum3,
  output Sum2,
  output Sum1,
  output Sum0
);

  wire fulladder_2_carryout, fulladder_3_carryout, fulladder_4_carryout;

  FullAdder fulladder_1 (.X(X3), .Y(Y3), .CarryIn(fulladder_2_carryout), .sum(Sum3), .CarryOut(Sum4));
  FullAdder fulladder_2 (.X(X2), .Y(Y2), .CarryIn(fulladder_3_carryout), .sum(Sum2), .CarryOut(fulladder_2_carryout));
  FullAdder fulladder_3 (.X(X1), .Y(Y1), .CarryIn(fulladder_4_carryout), .sum(Sum1), .CarryOut(fulladder_3_carryout));
  FullAdder fulladder_4 (.X(X0), .Y(Y0), .CarryIn(1'b0), .sum(Sum0), .CarryOut(fulladder_4_carryout));
endmodule

module _4_bit_Multiplier (
  input  Y3,
  input  Y2,
  input  Y1,
  input  Y0,
  input  X3,
  input  X2,
  input  X1,
  input  X0,
  output Z7,
  output Z6,
  output Z5,
  output Z4,
  output Z3,
  output Z2,
  output Z1,
  output Z0
);

  wire n4_bit_ripple_carry_adder_1_sum1, n4_bit_ripple_carry_adder_1_sum2, n4_bit_ripple_carry_adder_1_sum3,
       n4_bit_ripple_carry_adder_1_sum4, n4_bit_ripple_carry_adder_2_sum1, n4_bit_ripple_carry_adder_2_sum2,
       n4_bit_ripple_carry_adder_2_sum3, n4_bit_ripple_carry_adder_2_sum4, n4x1_multiplier_1_out1,
       n4x1_multiplier_1_out2, n4x1_multiplier_1_out3, n4x1_multiplier_2_out0, n4x1_multiplier_2_out1,
       n4x1_multiplier_2_out2, n4x1_multiplier_2_out3, n4x1_multiplier_3_out0, n4x1_multiplier_3_out1,
       n4x1_multiplier_3_out2, n4x1_multiplier_3_out3, n4x1_multiplier_4_out0, n4x1_multiplier_4_out1,
       n4x1_multiplier_4_out2, n4x1_multiplier_4_out3;

  _4x1_multiplier u_4x1_multiplier_1 (
    .Multiplier(Y0), .X3(X3), .X2(X2), .X1(X1), .X0(X0), .out0(Z0), .out1(n4x1_multiplier_1_out1),
    .out2(n4x1_multiplier_1_out2), .out3(n4x1_multiplier_1_out3));
  _4x1_multiplier u_4x1_multiplier_2 (
    .Multiplier(Y1), .X3(X3), .X2(X2), .X1(X1), .X0(X0), .out0(n4x1_multiplier_2_out0),
    .out1(n4x1_multiplier_2_out1), .out2(n4x1_multiplier_2_out2), .out3(n4x1_multiplier_2_out3));
  _4x1_multiplier u_4x1_multiplier_3 (
    .Multiplier(Y2), .X3(X3), .X2(X2), .X1(X1), .X0(X0), .out0(n4x1_multiplier_3_out0),
    .out1(n4x1_multiplier_3_out1), .out2(n4x1_multiplier_3_out2), .out3(n4x1_multiplier_3_out3));
  _4x1_multiplier u_4x1_multiplier_4 (
    .Multiplier(Y3), .X3(X3), .X2(X2), .X1(X1), .X0(X0), .out0(n4x1_multiplier_4_out0),
    .out1(n4x1_multiplier_4_out1), .out2(n4x1_multiplier_4_out2), .out3(n4x1_multiplier_4_out3));
  _4_bit_Ripple_Carry_Adder u_4_bit_ripple_carry_adder_1 (
    .Y3(n4x1_multiplier_2_out3), .X3(1'b0), .Y2(n4x1_multiplier_2_out2), .X2(n4x1_multiplier_1_out3),
    .Y1(n4x1_multiplier_2_out1), .X1(n4x1_multiplier_1_out2), .Y0(n4x1_multiplier_2_out0),
    .X0(n4x1_multiplier_1_out1), .Sum4(n4_bit_ripple_carry_adder_1_sum4),
    .Sum3(n4_bit_ripple_carry_adder_1_sum3), .Sum2(n4_bit_ripple_carry_adder_1_sum2),
    .Sum1(n4_bit_ripple_carry_adder_1_sum1), .Sum0(Z1));
  _4_bit_Ripple_Carry_Adder u_4_bit_ripple_carry_adder_2 (
    .Y3(n4x1_multiplier_3_out3), .X3(n4_bit_ripple_carry_adder_1_sum4), .Y2(n4x1_multiplier_3_out2),
    .X2(n4_bit_ripple_carry_adder_1_sum3), .Y1(n4x1_multiplier_3_out1),
    .X1(n4_bit_ripple_carry_adder_1_sum2), .Y0(n4x1_multiplier_3_out0),
    .X0(n4_bit_ripple_carry_adder_1_sum1), .Sum4(n4_bit_ripple_carry_adder_2_sum4),
    .Sum3(n4_bit_ripple_carry_adder_2_sum3), .Sum2(n4_bit_ripple_carry_adder_2_sum2),
    .Sum1(n4_bit_ripple_carry_adder_2_sum1), .Sum0(Z2));
  _4_bit_Ripple_Carry_Adder u_4_bit_ripple_carry_adder_3 (
    .Y3(n4x1_multiplier_4_out3), .X3(n4_bit_ripple_carry_adder_2_sum4), .Y2(n4x1_multiplier_4_out2),
    .X2(n4_bit_ripple_carry_adder_2_sum3), .Y1(n4x1_multiplier_4_out1),
    .X1(n4_bit_ripple_carry_adder_2_sum2), .Y0(n4x1_multiplier_4_out0),
    .X0(n4_bit_ripple_carry_adder_2_sum1), .Sum4(Z7), .Sum3(Z6), .Sum2(Z5), .Sum1(Z4), .Sum0(Z3));

  // Notes on the sheet:
  //   factor (4 bits)
  //   second factor (4 bits)
  //   product (7 bits)
  //   most significant (highest) bit
  //   least significant (lowest) bit
endmodule

module _3by2_divider (
  input  Y2,
  input  Y1,
  input  Y0,
  input  X1,
  input  X0,
  output Z2,
  output Z1,
  output Z0,
  output Error
);

  wire and_1_out, and_2_out, and_3_out, and_4_out, and_5_out, and_6_out, and_7_out, and_8_out, and_10_out,
       and_11_out, and_12_out, and_13_out, divide_by_2_1_z0, divide_by_2_1_z1, divide_by_2_1_z2,
       divide_by_3_1_z0, divide_by_3_1_z1, divide_by_3_1_z2, not_1_out, not_2_out, not_3_out, not_4_out;

  divide_by_3 divide_by_3_1 (
    .Z2(divide_by_3_1_z2), .Z1(divide_by_3_1_z1), .Z0(divide_by_3_1_z0), .X2(Y2), .X1(Y1), .X0(Y0));
  and and_1 (and_1_out, divide_by_3_1_z1, and_3_out);
  and and_2 (and_2_out, divide_by_3_1_z2, and_3_out);
  and and_3 (and_3_out, X1, X0);
  and and_4 (and_4_out, divide_by_3_1_z0, and_3_out);
  and and_5 (and_5_out, divide_by_2_1_z2, and_6_out);
  not not_1 (not_1_out, X0);
  divide_by_2 divide_by_2_1 (
    .Z2(divide_by_2_1_z2), .Z1(divide_by_2_1_z1), .Z0(divide_by_2_1_z0), .X2(Y2), .X1(Y1), .X0(Y0));
  and and_6 (and_6_out, X1, not_1_out);
  and and_7 (and_7_out, divide_by_2_1_z0, and_6_out);
  and and_8 (and_8_out, divide_by_2_1_z1, and_6_out);
  not not_2 (not_2_out, X1);
  not not_3 (not_3_out, X1);
  not not_4 (not_4_out, X0);
  and and_9 (Error, not_2_out, not_4_out);
  and and_10 (and_10_out, not_3_out, X0);
  and and_11 (and_11_out, Y2, and_10_out);
  or or_1 (Z2, and_2_out, and_5_out, and_11_out);
  or or_2 (Z1, and_1_out, and_8_out, and_12_out);
  and and_12 (and_12_out, Y1, and_10_out);
  and and_13 (and_13_out, Y0, and_10_out);
  or or_3 (Z0, and_4_out, and_7_out, and_13_out);

  // Notes on the sheet:
  //   Dividend (3 bits: Y2 Y1 Y0)
  //   Div3
  //   Div2
  //   Div0
  //   Div1
  //   Divisor (2 bits: X1 X0)
  //   Quotient (4 bits: Z2 Z1 Z0 and Error)
endmodule

module _2_bit_decoder (
  input  Input1,
  input  Input0,
  output Output3,
  output Output2,
  output Output1,
  output Output0
);

  wire not_1_out, not_2_out, not_3_out, not_4_out;

  and and_1 (Output3, Input1, Input0);
  not not_1 (not_1_out, Input0);
  and and_2 (Output2, Input1, not_1_out);
  not not_2 (not_2_out, Input0);
  not not_3 (not_3_out, Input1);
  not not_4 (not_4_out, Input1);
  and and_3 (Output1, not_4_out, Input0);
  and and_4 (Output0, not_3_out, not_2_out);
endmodule

module _4x1_multiplier (
  input  X3,
  input  X2,
  input  X1,
  input  X0,
  input  Multiplier,
  output out0,
  output out1,
  output out2,
  output out3
);

  and and_1 (out0, X0, Multiplier);
  and and_2 (out1, X1, Multiplier);
  and and_3 (out2, X2, Multiplier);
  and and_4 (out3, X3, Multiplier);
endmodule

module divide_by_2 (
  input  X2,
  input  X1,
  input  X0,
  output Z2,
  output Z1,
  output Z0
);


  assign Z0 = X1;
  assign Z1 = X2;
  assign Z2 = 1'b0;
endmodule

module divide_by_3 (
  input  X2,
  input  X1,
  input  X0,
  output Z2,
  output Z1,
  output Z0
);

  wire and_1_out, and_2_out, and_3_out, and_4_out, and_5_out, not_1_out, not_2_out, not_3_out, not_4_out,
       not_5_out;

  not not_1 (not_1_out, X0);
  and and_1 (and_1_out, X2, X1, not_1_out);
  and and_2 (and_2_out, X2, X1, X0);
  or or_1 (Z1, and_1_out, and_2_out);
  not not_2 (not_2_out, X2);
  and and_3 (and_3_out, not_2_out, X1, X0);
  not not_3 (not_3_out, X1);
  not not_4 (not_4_out, X0);
  and and_4 (and_4_out, X2, not_3_out, not_4_out);
  or or_2 (Z0, and_3_out, and_4_out, and_5_out);
  not not_5 (not_5_out, X1);
  and and_5 (and_5_out, X2, not_5_out, X0);

  assign Z2 = 1'b0;
endmodule
